// Logisim project Organizacion de Computadores (Proyecto 2).circ as structural Verilog
module HalfAdder (
  input  A,
  input  B,
  output Sum,
  output Carry
);

  xor xor_1 (Sum, A, B);
  and and_1 (Carry, A, B);
endmodule

module FullAdder (
  input  A,
  input  B,
  input  CIn,
  output COut,
  output Sum
);

  wire halfadder_1_carry, halfadder_1_sum, halfadder_2_carry;

  HalfAdder halfadder_1 (.A(A), .B(B), .Sum(halfadder_1_sum), .Carry(halfadder_1_carry));
  HalfAdder halfadder_2 (.A(halfadder_1_sum), .B(CIn), .Sum(Sum), .Carry(halfadder_2_carry));
  or or_1 (COut, halfadder_1_carry, halfadder_2_carry);
endmodule

module Add16 (
  input  [15:0] X,
  input  [15:0] Y,
  output [15:0] Out,
  output Overflow
);

  wire fulladder_1_cout, fulladder_2_cout, fulladder_3_cout, fulladder_4_cout, fulladder_5_cout,
       fulladder_6_cout, fulladder_7_cout, fulladder_8_cout, fulladder_9_cout, fulladder_10_cout,
       fulladder_11_cout, fulladder_12_cout, fulladder_13_cout, fulladder_14_cout, fulladder_15_cout;

  FullAdder fulladder_1 (.A(X[0]), .B(Y[0]), .CIn(1'b0), .COut(fulladder_1_cout), .Sum(Out[0]));
  FullAdder fulladder_2 (.A(X[1]), .B(Y[1]), .CIn(fulladder_1_cout), .COut(fulladder_2_cout), .Sum(Out[1]));
  FullAdder fulladder_3 (.A(X[2]), .B(Y[2]), .CIn(fulladder_2_cout), .COut(fulladder_3_cout), .Sum(Out[2]));
  FullAdder fulladder_4 (.A(X[3]), .B(Y[3]), .CIn(fulladder_3_cout), .COut(fulladder_4_cout), .Sum(Out[3]));
  FullAdder fulladder_5 (.A(X[4]), .B(Y[4]), .CIn(fulladder_4_cout), .COut(fulladder_5_cout), .Sum(Out[4]));
  FullAdder fulladder_6 (.A(X[5]), .B(Y[5]), .CIn(fulladder_5_cout), .COut(fulladder_6_cout), .Sum(Out[5]));
  FullAdder fulladder_7 (.A(X[6]), .B(Y[6]), .CIn(fulladder_6_cout), .COut(fulladder_7_cout), .Sum(Out[6]));
  FullAdder fulladder_8 (.A(X[7]), .B(Y[7]), .CIn(fulladder_7_cout), .COut(fulladder_8_cout), .Sum(Out[7]));
  FullAdder fulladder_9 (.A(X[8]), .B(Y[8]), .CIn(fulladder_8_cout), .COut(fulladder_9_cout), .Sum(Out[8]));
  FullAdder fulladder_10 (.A(X[9]), .B(Y[9]), .CIn(fulladder_9_cout), .COut(fulladder_10_cout), .Sum(Out[9]));
  FullAdder fulladder_11 (.A(X[10]), .B(Y[10]), .CIn(fulladder_10_cout), .COut(fulladder_11_cout), .Sum(Out[10]));
  FullAdder fulladder_12 (.A(X[11]), .B(Y[11]), .CIn(fulladder_11_cout), .COut(fulladder_12_cout), .Sum(Out[11]));
  FullAdder fulladder_13 (.A(X[12]), .B(Y[12]), .CIn(fulladder_12_cout), .COut(fulladder_13_cout), .Sum(Out[12]));
  FullAdder fulladder_14 (.A(X[13]), .B(Y[13]), .CIn(fulladder_13_cout), .COut(fulladder_14_cout), .Sum(Out[13]));
  FullAdder fulladder_15 (.A(X[14]), .B(Y[14]), .CIn(fulladder_14_cout), .COut(fulladder_15_cout), .Sum(Out[14]));
  FullAdder fulladder_16 (.A(X[15]), .B(Y[15]), .CIn(fulladder_15_cout), .COut(Overflow), .Sum(Out[15]));
endmodule

module Inc16 (
  input  [15:0] In,
  output [15:0] Out,
  output Overflow
);

  Add16 add16_1 (.X(In), .Y(16'h1), .Out(Out), .Overflow(Overflow));
endmodule
