// Logisim project Organizacion de Computadores (Proyecto 3).circ as structural Verilog
module Bit (
  input  in_1,
  input  in_2,
  output out_3
);

  wire clock_1_out, multiplexer_1_out;

  Multiplexer multiplexer_1 (.in0(out_3), .in1(in_1), .out(multiplexer_1_out), .sel(in_2));  // open: en
  Clock clock_1 (.out(clock_1_out));
  D_Flip_Flop d_ff_1 (.clk(clock_1_out), .D(multiplexer_1_out), .Q(out_3));  // open: Qn, preset, en, reset
endmodule

module Register (
  input  [15:0] In,
  input  Load,
  output [15:0] Out
);

  wire clock_1_out;
  wire [15:0] multiplexer_1_out;

  Clock clock_1 (.out(clock_1_out));
  Multiplexer #(.width(16)) multiplexer_1 (.in0(Out), .in1(In), .out(multiplexer_1_out), .sel(Load));  // open: en
  D_Flip_Flop d_ff_1 (.clk(clock_1_out), .D(multiplexer_1_out[0]), .Q(Out[0]));  // open: Qn, preset, en, reset
  D_Flip_Flop d_ff_2 (.clk(clock_1_out), .D(multiplexer_1_out[1]), .Q(Out[1]));  // open: Qn, preset, en, reset
  D_Flip_Flop d_ff_3 (.clk(clock_1_out), .D(multiplexer_1_out[2]), .Q(Out[2]));  // open: Qn, preset, en, reset
  D_Flip_Flop d_ff_4 (.clk(clock_1_out), .D(multiplexer_1_out[3]), .Q(Out[3]));  // open: Qn, preset, en, reset
  D_Flip_Flop d_ff_5 (.clk(clock_1_out), .D(multiplexer_1_out[4]), .Q(Out[4]));  // open: Qn, preset, en, reset
  D_Flip_Flop d_ff_6 (.clk(clock_1_out), .D(multiplexer_1_out[5]), .Q(Out[5]));  // open: Qn, preset, en, reset
  D_Flip_Flop d_ff_7 (.clk(clock_1_out), .D(multiplexer_1_out[6]), .Q(Out[6]));  // open: Qn, preset, en, reset
  D_Flip_Flop d_ff_8 (.clk(clock_1_out), .D(multiplexer_1_out[7]), .Q(Out[7]));  // open: Qn, preset, en, reset
  D_Flip_Flop d_ff_9 (.clk(clock_1_out), .D(multiplexer_1_out[8]), .Q(Out[8]));  // open: Qn, preset, en, reset
  D_Flip_Flop d_ff_10 (.clk(clock_1_out), .D(multiplexer_1_out[9]), .Q(Out[9]));  // open: Qn, preset, en, reset
  D_Flip_Flop d_ff_11 (.clk(clock_1_out), .D(multiplexer_1_out[10]), .Q(Out[10]));  // open: Qn, preset, en, reset
  D_Flip_Flop d_ff_12 (.clk(clock_1_out), .D(multiplexer_1_out[11]), .Q(Out[11]));  // open: Qn, preset, en, reset
  D_Flip_Flop d_ff_13 (.clk(clock_1_out), .D(multiplexer_1_out[12]), .Q(Out[12]));  // open: Qn, preset, en, reset
  D_Flip_Flop d_ff_14 (.clk(clock_1_out), .D(multiplexer_1_out[13]), .Q(Out[13]));  // open: Qn, preset, en, reset
  D_Flip_Flop d_ff_15 (.clk(clock_1_out), .D(multiplexer_1_out[14]), .Q(Out[14]));  // open: Qn, preset, en, reset
  D_Flip_Flop d_ff_16 (.clk(clock_1_out), .D(multiplexer_1_out[15]), .Q(Out[15]));  // open: Qn, preset, en, reset
endmodule

module Ram8 (
  input  Load,
  input  [2:0] Address,
  input  [15:0] In,
  output [15:0] Out
);

  wire clock_1_out, demultiplexer_1_out0, demultiplexer_1_out1, demultiplexer_1_out2, demultiplexer_1_out3,
       demultiplexer_1_out4, demultiplexer_1_out5, demultiplexer_1_out6, demultiplexer_1_out7;
  wire [15:0] register_1_q, register_2_q, register_3_q, register_4_q, register_5_q, register_6_q,
       register_7_q, register_8_q;

  Demultiplexer #(.select(3), .enable("false")) demultiplexer_1 (
    .out0(demultiplexer_1_out0), .out1(demultiplexer_1_out1), .out2(demultiplexer_1_out2),
    .out3(demultiplexer_1_out3), .out4(demultiplexer_1_out4), .out5(demultiplexer_1_out5),
    .out6(demultiplexer_1_out6), .out7(demultiplexer_1_out7), .in(Load), .sel(Address));
  Clock clock_1 (.out(clock_1_out));
  Register_part #(.width(16)) register_1 (
    .D(In), .en(demultiplexer_1_out0), .Q(register_1_q), .clk(clock_1_out));  // open: clr
  Register_part #(.width(16)) register_2 (
    .D(In), .en(demultiplexer_1_out1), .Q(register_2_q), .clk(clock_1_out));  // open: clr
  Register_part #(.width(16)) register_3 (
    .D(In), .en(demultiplexer_1_out2), .Q(register_3_q), .clk(clock_1_out));  // open: clr
  Register_part #(.width(16)) register_4 (
    .D(In), .en(demultiplexer_1_out3), .Q(register_4_q), .clk(clock_1_out));  // open: clr
  Register_part #(.width(16)) register_5 (
    .D(In), .en(demultiplexer_1_out4), .Q(register_5_q), .clk(clock_1_out));  // open: clr
  Register_part #(.width(16)) register_6 (
    .D(In), .en(demultiplexer_1_out5), .Q(register_6_q), .clk(clock_1_out));  // open: clr
  Register_part #(.width(16)) register_7 (
    .D(In), .en(demultiplexer_1_out6), .Q(register_7_q), .clk(clock_1_out));  // open: clr
  Register_part #(.width(16)) register_8 (
    .D(In), .en(demultiplexer_1_out7), .Q(register_8_q), .clk(clock_1_out));  // open: clr
  Multiplexer #(.select(3), .width(16), .enable("false")) multiplexer_1 (
    .in0(register_1_q), .in1(register_2_q), .in2(register_3_q), .in3(register_4_q), .in4(register_5_q),
    .in5(register_6_q), .in6(register_7_q), .in7(register_8_q), .out(Out), .sel(Address));
endmodule

module Ram64 (
  input  [15:0] In,
  input  [5:0] Address,
  input  Load,
  output [15:0] Out
);

  wire demultiplexer_1_out0, demultiplexer_1_out1, demultiplexer_1_out2, demultiplexer_1_out3,
       demultiplexer_1_out4, demultiplexer_1_out5, demultiplexer_1_out6, demultiplexer_1_out7;
  wire [15:0] RAM_0_out, RAM_1_out, RAM_2_out, RAM_3_out, RAM_4_out, RAM_5_out, RAM_6_out, RAM_7_out;

  Demultiplexer #(.select(3), .enable("false")) demultiplexer_1 (
    .out0(demultiplexer_1_out0), .out1(demultiplexer_1_out1), .out2(demultiplexer_1_out2),
    .out3(demultiplexer_1_out3), .out4(demultiplexer_1_out4), .out5(demultiplexer_1_out5),
    .out6(demultiplexer_1_out6), .out7(demultiplexer_1_out7), .in(Load), .sel(Address[5:3]));
  Ram8 RAM_0 (.Load(demultiplexer_1_out0), .Address(Address[2:0]), .In(In), .Out(RAM_0_out));
  Ram8 RAM_1 (.Load(demultiplexer_1_out1), .Address(Address[2:0]), .In(In), .Out(RAM_1_out));
  Ram8 RAM_2 (.Load(demultiplexer_1_out2), .Address(Address[2:0]), .In(In), .Out(RAM_2_out));
  Ram8 RAM_3 (.Load(demultiplexer_1_out3), .Address(Address[2:0]), .In(In), .Out(RAM_3_out));
  Ram8 RAM_4 (.Load(demultiplexer_1_out4), .Address(Address[2:0]), .In(In), .Out(RAM_4_out));
  Ram8 RAM_5 (.Load(demultiplexer_1_out5), .Address(Address[2:0]), .In(In), .Out(RAM_5_out));
  Ram8 RAM_6 (.Load(demultiplexer_1_out6), .Address(Address[2:0]), .In(In), .Out(RAM_6_out));
  Ram8 RAM_7 (.Load(demultiplexer_1_out7), .Address(Address[2:0]), .In(In), .Out(RAM_7_out));
  Multiplexer #(.select(3), .width(16), .enable("false")) multiplexer_1 (
    .in0(RAM_0_out), .in1(RAM_1_out), .in2(RAM_2_out), .in3(RAM_3_out), .in4(RAM_4_out), .in5(RAM_5_out),
    .in6(RAM_6_out), .in7(RAM_7_out), .out(Out), .sel(Address[5:3]));
endmodule

module Ram512 (
  input  [15:0] In,
  input  Load,
  input  [8:0] Address,
  output [15:0] Out
);

  wire demultiplexer_1_out0, demultiplexer_1_out1, demultiplexer_1_out2, demultiplexer_1_out3,
       demultiplexer_1_out4, demultiplexer_1_out5, demultiplexer_1_out6, demultiplexer_1_out7;
  wire [15:0] ram64_1_out, ram64_2_out, ram64_3_out, ram64_4_out, ram64_5_out, ram64_6_out, ram64_7_out,
       ram64_8_out;

  Demultiplexer #(.select(3), .enable("false")) demultiplexer_1 (
    .out0(demultiplexer_1_out0), .out1(demultiplexer_1_out1), .out2(demultiplexer_1_out2),
    .out3(demultiplexer_1_out3), .out4(demultiplexer_1_out4), .out5(demultiplexer_1_out5),
    .out6(demultiplexer_1_out6), .out7(demultiplexer_1_out7), .in(Load), .sel(Address[8:6]));
  Ram64 ram64_1 (.In(In), .Address(Address[5:0]), .Load(demultiplexer_1_out0), .Out(ram64_1_out));
  Ram64 ram64_2 (.In(In), .Address(Address[5:0]), .Load(demultiplexer_1_out1), .Out(ram64_2_out));
  Ram64 ram64_3 (.In(In), .Address(Address[5:0]), .Load(demultiplexer_1_out2), .Out(ram64_3_out));
  Ram64 ram64_4 (.In(In), .Address(Address[5:0]), .Load(demultiplexer_1_out3), .Out(ram64_4_out));
  Ram64 ram64_5 (.In(In), .Address(Address[5:0]), .Load(demultiplexer_1_out4), .Out(ram64_5_out));
  Ram64 ram64_6 (.In(In), .Address(Address[5:0]), .Load(demultiplexer_1_out5), .Out(ram64_6_out));
  Ram64 ram64_7 (.In(In), .Address(Address[5:0]), .Load(demultiplexer_1_out6), .Out(ram64_7_out));
  Ram64 ram64_8 (.In(In), .Address(Address[5:0]), .Load(demultiplexer_1_out7), .Out(ram64_8_out));
  Multiplexer #(.select(3), .width(16), .enable("false")) multiplexer_1 (
    .in0(ram64_1_out), .in1(ram64_2_out), .in2(ram64_3_out), .in3(ram64_4_out), .in4(ram64_5_out),
    .in5(ram64_6_out), .in6(ram64_7_out), .in7(ram64_8_out), .out(Out), .sel(Address[8:6]));
endmodule
