// Logisim project Organizacion de computadores (Proyecto 1).circ as structural Verilog: 15 circuits, main circuit Multiplexor
module Multiplexor (
  input  B,
  input  Sel,
  input  A,
  output out_4
);

  wire and_1_out, and_2_out, not_1_out;

  not not_1 (not_1_out, Sel);
  and and_1 (and_1_out, B, Sel);
  and and_2 (and_2_out, not_1_out, A);
  or or_1 (out_4, and_1_out, and_2_out);
endmodule

module Demultiplexor (
  input  Sel,
  input  In,
  output y0,
  output y1
);

  wire not_1_out;

  not not_1 (not_1_out, Sel);
  and and_1 (y0, not_1_out, In);
  and and_2 (y1, Sel, In);
endmodule

module Not16 (
  input  [15:0] in_1,
  input  [15:0] in_2,
  output [15:0] out_3,
  output [15:0] out_4
);

  not not_1 (out_3[0], in_1[0]);
  not not_2 (out_3[1], in_1[1]);
  not not_3 (out_3[2], in_1[2]);
  not not_4 (out_3[3], in_1[3]);
  not not_5 (out_3[4], in_1[4]);
  not not_6 (out_3[5], in_1[5]);
  not not_7 (out_3[6], in_1[6]);
  not not_8 (out_3[7], in_1[7]);
  not not_9 (out_3[8], in_1[8]);
  not not_10 (out_3[9], in_1[9]);
  not not_11 (out_3[10], in_1[10]);
  not not_12 (out_3[11], in_1[11]);
  not not_13 (out_3[12], in_1[12]);
  not not_14 (out_3[13], in_1[13]);
  not not_15 (out_3[14], in_1[14]);
  not not_16 (out_3[15], in_1[15]);
  assign out_4 = ~in_2;  // NOT_Gate not_17, 16 bits wide
endmodule

module Not (
  input  in_1,
  output out_2
);

  nand nand_1 (out_2, in_1, in_1);
endmodule

module And (
  input  in_1,
  input  in_2,
  output out_3
);

  wire nand_1_out;

  nand nand_1 (nand_1_out, in_1, in_2);
  nand nand_2 (out_3, nand_1_out, nand_1_out);
endmodule

module Or (
  input  in_1,
  input  in_2,
  output out_3
);

  wire not_1_out, not_2_out;

  not not_1 (not_1_out, in_1);
  not not_2 (not_2_out, in_2);
  nand nand_1 (out_3, not_1_out, not_2_out);
endmodule

module Xor (
  input  in_1,
  input  in_2,
  output out_3
);

  wire and_1_out, and_2_out, not_1_out, not_2_out;

  not not_1 (not_1_out, in_1);
  not not_2 (not_2_out, in_2);
  and and_1 (and_1_out, in_1, not_2_out);
  and and_2 (and_2_out, not_1_out, in_2);
  or or_1 (out_3, and_1_out, and_2_out);
endmodule

module And16 (
  input  [15:0] in_1,
  input  [15:0] in_2,
  output [15:0] out_3
);

  assign out_3 = in_1 & in_2;  // AND_Gate and_1, 16 bits wide
endmodule

module Or16 (
  input  [15:0] in_1,
  input  [15:0] in_2,
  output [15:0] out_3
);

  assign out_3 = in_1 | in_2;  // OR_Gate or_1, 16 bits wide
endmodule

module Mux16 (
  input  [15:0] in_1,
  input  [15:0] in_2,
  input  in_3,
  output [15:0] out_4
);

  Multiplexer #(.width(16)) multiplexer_1 (.in0(in_1), .in1(in_2), .out(out_4), .sel(in_3));  // open: en
endmodule

module Or8Way (
  input  [7:0] in_1,
  output out_2
);

  wire or_1_out, or_2_out, or_3_out, or_4_out, or_5_out, or_6_out;

  or or_1 (or_1_out, in_1[0], in_1[1]);
  or or_2 (or_2_out, in_1[2], in_1[3]);
  or or_3 (or_3_out, in_1[4], in_1[5]);
  or or_4 (or_4_out, in_1[6], in_1[7]);
  or or_5 (or_5_out, or_1_out, or_2_out);
  or or_6 (or_6_out, or_3_out, or_4_out);
  or or_7 (out_2, or_5_out, or_6_out);
endmodule

module Mux4Way16 (
  input  [15:0] in_1,
  input  [15:0] in_2,
  input  [1:0] in_3,
  input  [15:0] in_4,
  input  [15:0] in_5,
  output [15:0] out_6
);

  wire [15:0] multiplexer_1_out, multiplexer_2_out;

  Multiplexer #(.width(16)) multiplexer_1 (.in0(in_1), .in1(in_2), .out(multiplexer_1_out), .sel(in_3[0]));  // open: en
  Multiplexer #(.width(16)) multiplexer_2 (.in0(in_4), .in1(in_5), .out(multiplexer_2_out), .sel(in_3[0]));  // open: en
  Multiplexer #(.width(16)) multiplexer_3 (
    .in0(multiplexer_1_out), .in1(multiplexer_2_out), .out(out_6), .sel(in_3[1]));  // open: en
endmodule

module Mux8Way16 (
  input  [15:0] in_1,
  input  [15:0] in_2,
  input  [15:0] in_3,
  input  [15:0] in_4,
  input  [15:0] in_5,
  input  [15:0] in_6,
  input  [15:0] in_7,
  input  [15:0] in_8,
  input  [2:0] in_9,
  output [15:0] out_10
);

  wire [15:0] multiplexer_1_out, multiplexer_2_out;

  Multiplexer #(.select(2), .width(16)) multiplexer_1 (
    .in0(in_1), .in1(in_2), .in2(in_3), .in3(in_4), .out(multiplexer_1_out), .sel(in_9[1:0]));  // open: en
  Multiplexer #(.select(2), .width(16)) multiplexer_2 (
    .in0(in_5), .in1(in_6), .in2(in_7), .in3(in_8), .out(multiplexer_2_out), .sel(in_9[1:0]));  // open: en
  Multiplexer #(.width(16)) multiplexer_3 (
    .in0(multiplexer_1_out), .in1(multiplexer_2_out), .out(out_10), .sel(in_9[2]));  // open: en
endmodule

module DMux4Way (
  input  in_1,
  input  [1:0] in_2,
  output out_3,
  output out_4,
  output out_5,
  output out_6
);

  wire demultiplexer_1_out0, demultiplexer_1_out1;

  Demultiplexer demultiplexer_1 (
    .out0(demultiplexer_1_out0), .out1(demultiplexer_1_out1), .in(in_1), .sel(in_2[1]));  // open: en
  Demultiplexer demultiplexer_2 (.out0(out_3), .out1(out_4), .in(demultiplexer_1_out0), .sel(in_2[0]));  // open: en
  Demultiplexer demultiplexer_3 (.out0(out_5), .out1(out_6), .in(demultiplexer_1_out1), .sel(in_2[0]));  // open: en
endmodule

module DMux8Way (
  input  in_1,
  input  [2:0] in_2,
  output out_3,
  output out_4,
  output out_5,
  output out_6,
  output out_7,
  output out_8,
  output out_9,
  output out_10
);

  wire demultiplexer_1_out0, demultiplexer_1_out1;

  Demultiplexer demultiplexer_1 (
    .out0(demultiplexer_1_out0), .out1(demultiplexer_1_out1), .in(in_1), .sel(in_2[2]));  // open: en
  Demultiplexer #(.select(2)) demultiplexer_2 (
    .out0(out_3), .out1(out_4), .out2(out_5), .out3(out_6), .in(demultiplexer_1_out0), .sel(in_2[1:0]));  // open: en
  Demultiplexer #(.select(2)) demultiplexer_3 (
    .out0(out_7), .out1(out_8), .out2(out_9), .out3(out_10), .in(demultiplexer_1_out1), .sel(in_2[1:0]));  // open: en
endmodule
